# Fritzing sketch WiringDiagram (saved by Fritzing 0.9.10b)

parts:
  ESP32-C3 = Adafruit QT Py ESP32-C3 rev A
  1K_Resistor = Resistor [tolerance=±5% power=0.25 resistance=1k package=THT]
  IR_Receiver = LED - 3mm [color="Infrared (940nm)" current=0.030 package="3 mm [THT]"]
  IR_Transmitter = LED - 3mm [color="Infrared (850nm)" current=0.030 package="3 mm [THT]"]
  2K_Resistor = Resistor [tolerance=±5% power=0.25 resistance=2k package=THT]
  Front_Button = Pushbutton [package="[THT]"]
  Back_Button = Pushbutton [package="[THT]"]
  I2C_Display = Grove OLED 128x96

nets:
  N1: ESP32-C3.A0, IR_Receiver.anode, 2K_Resistor.Pin_1
  N2: ESP32-C3.A2, 2K_Resistor.Pin_0, Back_Button.Pin_3, Back_Button.Pin_4
  N3: ESP32-C3.SDA, I2C_Display.SCL
  N4: ESP32-C3.SCL, I2C_Display.SDA
  N5: ESP32-C3.TX, IR_Transmitter.anode
  N6: ESP32-C3.RX, Front_Button.Pin_4
  N7: ESP32-C3.3.3V, IR_Receiver.cathode
  N8: 1K_Resistor.Pin_1, IR_Transmitter.cathode
